// Logisim project 2107086_Cache.circ as structural Verilog: 2 circuits, main circuit main
module main (
  input  [4:0] Address__MAR,
  input  Decition,
  input  Start_Copy,
  input  EnRAM,
  input  LdCache,
  output [17:0] Data__MBR
);

  wire clock_1_out, control_block_copy_1_cachew, control_block_copy_1_clrcnt, control_block_copy_1_inccnt,
       control_block_copy_1_ramr, control_block_copy_1_selcnt, demultiplexer_1_out0, demultiplexer_1_out1,
       demultiplexer_2_out0, demultiplexer_2_out1, or_1_out, or_2_out;
  wire [1:0] counter_1_q, multiplexer_1_out;

  Clock clock_1 (.out(clock_1_out));
  Control_block_copy control_block_copy_1 (
    .Clk(clock_1_out), .St_Cp(Start_Copy), .in_3(counter_1_q), .CacheW(control_block_copy_1_cachew),
    .RAMR(control_block_copy_1_ramr), .IncCnt(control_block_copy_1_inccnt),
    .SelCnt(control_block_copy_1_selcnt), .CLRCnt(control_block_copy_1_clrcnt));
  Multiplexer #(.width(2), .enable("false")) multiplexer_1 (
    .in0(Address__MAR[1:0]), .in1(counter_1_q), .out(multiplexer_1_out), .sel(control_block_copy_1_selcnt));
  Counter #(.width(2), .max('h3)) counter_1 (
    .count(control_block_copy_1_inccnt), .Q(counter_1_q), .clk(clock_1_out), .clr(control_block_copy_1_clrcnt));  // open: load, D, carry
  Demultiplexer #(.enable("false")) demultiplexer_1 (
    .out0(demultiplexer_1_out0), .out1(demultiplexer_1_out1), .in(or_1_out), .sel(Decition));
  or or_1 (or_1_out, control_block_copy_1_cachew, LdCache);
  RAM #(.addrWidth(4), .dataWidth(18), .bus("separate")) ram_1 (
    .addr({Address__MAR[3:2], multiplexer_1_out}), .din(Data__MBR), .data(Data__MBR),
    .str(demultiplexer_1_out0), .clk(clock_1_out), .ld(demultiplexer_2_out1));  // open: sel, clr
  Demultiplexer #(.enable("false")) demultiplexer_2 (
    .out0(demultiplexer_2_out0), .out1(demultiplexer_2_out1), .in(or_2_out), .sel(Decition));
  or or_2 (or_2_out, control_block_copy_1_ramr, EnRAM);
  RAM #(.addrWidth(5), .dataWidth(18), .bus("separate")) ram_2 (
    .addr({Address__MAR[4:2], multiplexer_1_out}), .din(Data__MBR), .data(Data__MBR),
    .str(demultiplexer_1_out1), .clk(clock_1_out), .ld(demultiplexer_2_out0));  // open: sel, clr

  // Notes on the sheet:
  //   _____________
  //   |  1  |   1   |   2    |
  //   _____________
  //   |tag|block|offset|
  //   _____________
  //   Let, 1 block of memory contains 4 Byte of information
  //   So, the main memory has 4 blocks and the cache memory has two blocks
  //   16 Byte Cache (16x8)
  //   32 Byte RAM (32x8))
endmodule

// R2C_copy
module Control_block_copy (
  input  Clk,
  input  St_Cp,
  input  [1:0] in_3,
  output CacheW,
  output RAMR,
  output IncCnt,
  output SelCnt,
  output CLRCnt
);

  wire multiplexer_1_out, not_1_out, not_2_out, or_1_out;
  wire [1:0] counter_1_q, rom_1_data_2;
  wire [7:0] rom_1_data;

  Counter #(.width(2), .max('h3)) counter_1 (
    .load(not_1_out), .D(rom_1_data[1:0]), .count(multiplexer_1_out), .Q(counter_1_q), .clk(Clk));  // open: carry, clr
  not not_1 (not_1_out, multiplexer_1_out);
  Multiplexer #(.select(2), .enable("false")) multiplexer_1 (
    .in0(1'b0), .in1(1'b1), .in2(not_2_out), .in3(St_Cp), .out(multiplexer_1_out), .sel(rom_1_data_2));
  ROM #(.addrWidth(2), .dataWidth(10)) rom_1 (
    .addr(counter_1_q),
    .data({CLRCnt, SelCnt, rom_1_data[7], IncCnt, rom_1_data[5:4], rom_1_data_2, rom_1_data[1:0]}));  // open: sel
  not not_2 (not_2_out, or_1_out);
  or or_1 (or_1_out, in_3[0], in_3[1]);
  assign CacheW = 1'b1 ? rom_1_data[4] : 1'bz;  // Controlled_Buffer controlled_buffer_1
  assign RAMR = 1'b1 ? rom_1_data[5] : 1'bz;  // Controlled_Buffer controlled_buffer_2

  // Notes on the sheet:
  //   contents of rom_1 (hex, n*v repeats v):
  //   20c 1f4 1fa
endmodule
