// Logisim project 3 bit downcounter .circ as structural Verilog: 2 circuits, main circuit main
module down_counter_f9b3b6f1 (
  output out_1,
  output out_2,
  output out_3
);

  wire clock_1_out, DA0_qn, or_1_out, xnor_1_out, xnor_2_out;

  Clock clock_1 (.out(clock_1_out));
  D_Flip_Flop DA0 (.clk(clock_1_out), .D(DA0_qn), .Q(out_3), .Qn(DA0_qn));  // open: preset, reset
  xnor xnor_1 (xnor_1_out, out_3, out_2);
  D_Flip_Flop DA1 (.preset(xnor_1_out), .reset(xnor_1_out));  // open: D, clk, Q, Qn
  or or_1 (or_1_out, out_2, out_3);
  D_Flip_Flop DA2 (.preset(out_1), .reset(out_1));  // open: D, clk, Q, Qn
  xnor xnor_2 (xnor_2_out, out_1, or_1_out);
endmodule

module main (
);


  // Notes on the sheet:
  //   2107086
endmodule
