// Logisim project 4 bit comparator 2107086.circ as structural Verilog: 5 circuits, main circuit main
module main (
  input  D,
  input  C,
  input  B,
  input  A
);

  wire bcd_to_hex_7_segment_1_a_2, bcd_to_hex_7_segment_1_b_2, bcd_to_hex_7_segment_1_c_2,
       bcd_to_hex_7_segment_1_d_2, bcd_to_hex_7_segment_1_e, bcd_to_hex_7_segment_1_f,
       bcd_to_hex_7_segment_1_g;

  BCD_to_Hex_7_Segment bcd_to_hex_7_segment_1 (
    .A(A), .B(B), .C(C), .D(D), .a_2(bcd_to_hex_7_segment_1_a_2), .b_2(bcd_to_hex_7_segment_1_b_2),
    .c_2(bcd_to_hex_7_segment_1_c_2), .d_2(bcd_to_hex_7_segment_1_d_2), .e(bcd_to_hex_7_segment_1_e),
    .f(bcd_to_hex_7_segment_1_f), .g(bcd_to_hex_7_segment_1_g));
  _7_Segment_Display u_7_segment_display_1 (
    .g(bcd_to_hex_7_segment_1_g), .f(bcd_to_hex_7_segment_1_f), .a(bcd_to_hex_7_segment_1_a_2),
    .b(bcd_to_hex_7_segment_1_b_2), .e(bcd_to_hex_7_segment_1_e), .d(bcd_to_hex_7_segment_1_d_2),
    .c(bcd_to_hex_7_segment_1_c_2));  // open: dp

  // Notes on the sheet:
  //   2107086
endmodule

module BCD_to_Hex_7_Segment (
  input  A,
  input  B,
  input  C,
  input  D,
  output a_2,
  output b_2,
  output c_2,
  output d_2,
  output e,
  output f,
  output g
);

  wire A_prime_B_out, A_prime_B_prime_C_out, A_prime_B_prime_out, A_prime_BC_prime_out, A_prime_BD_out,
       A_prime_C_out, A_prime_CD_out, A_prime_CD_prime_out, A_prime_D_out, AB_prime_C_prime_out,
       AB_prime_D_out, AB_prime_out, ABD_out, AC_out, AC_prime_out, AD_out, AD_prime_out, B_prime_C_out,
       B_prime_C_prime_D_prime_out, B_prime_D_prime_out, BC_out, BC_prime_D_out, BCD_prime_out, BD_prime_out,
       C_prime_D_prime_2_out, C_prime_D_prime_out, CD_prime_out, not_1_out, not_2_out, not_3_out, not_4_out;

  not not_1 (not_1_out, A);
  not not_2 (not_2_out, B);
  not not_3 (not_3_out, C);
  not not_4 (not_4_out, D);
  and B_prime_D_prime (B_prime_D_prime_out, not_2_out, not_4_out);
  and A_prime_C (A_prime_C_out, not_1_out, C);
  and BC (BC_out, B, C);
  and AD_prime (AD_prime_out, A, not_4_out);
  and AB_prime_C_prime (AB_prime_C_prime_out, A, not_2_out, not_3_out);
  and A_prime_BD (A_prime_BD_out, not_1_out, B, D);
  and AC_prime (AC_prime_out, A, not_3_out);
  and A_prime_B_prime (A_prime_B_prime_out, not_1_out, not_2_out);
  and C_prime_D_prime (C_prime_D_prime_out, not_3_out, not_4_out);
  and A_prime_CD (A_prime_CD_out, not_1_out, C, D);
  and A_prime_D (A_prime_D_out, not_1_out, D);
  and A_prime_B (A_prime_B_out, not_1_out, B);
  and AB_prime (AB_prime_out, A, not_2_out);
  and B_prime_C_prime_D_prime (B_prime_C_prime_D_prime_out, not_2_out, not_3_out, not_4_out);
  and A_prime_B_prime_C (A_prime_B_prime_C_out, not_1_out, not_2_out, C);
  and A_prime_CD_prime (A_prime_CD_prime_out, not_1_out, C, not_4_out);
  and BC_prime_D (BC_prime_D_out, B, not_3_out, D);
  and BCD_prime (BCD_prime_out, B, C, not_4_out);
  and AB_prime_D (AB_prime_D_out, A, not_2_out, D);
  and CD_prime (CD_prime_out, C, not_4_out);
  and AC (AC_out, A, C);
  and ABD (ABD_out, A, B, D);
  and A_prime_BC_prime (A_prime_BC_prime_out, not_1_out, B, not_3_out);
  and C_prime_D_prime_2 (C_prime_D_prime_2_out, not_3_out, not_4_out);
  and BD_prime (BD_prime_out, B, not_4_out);
  and AD (AD_out, A, D);
  and B_prime_C (B_prime_C_out, not_2_out, C);
  or u_a (a_2, B_prime_D_prime_out, A_prime_C_out, BC_out, AD_prime_out, AB_prime_C_prime_out, A_prime_BD_out);
  or u_b (b_2, AC_prime_out, B_prime_D_prime_out, A_prime_B_prime_out, C_prime_D_prime_out, A_prime_CD_out);
  or u_c (c_2, not_3_out, A_prime_D_out, A_prime_B_out, AB_prime_out);
  or u_d (d_2, B_prime_C_prime_D_prime_out, A_prime_B_prime_C_out, A_prime_CD_prime_out, AC_prime_out, BC_prime_D_out, BCD_prime_out, AB_prime_D_out);
  or u_e (e, B_prime_D_prime_out, CD_prime_out, AC_out, ABD_out);
  or u_f (f, AB_prime_out, BD_prime_out, AC_out, A_prime_BC_prime_out, C_prime_D_prime_2_out);
  or u_g (g, A_prime_BC_prime_out, CD_prime_out, AB_prime_out, AD_out, B_prime_C_out);

  // Notes on the sheet:
  //   2107086
endmodule

module ExOR (
  input  A,
  input  B,
  output A_prime_B,
  output A_ExOR_B,
  output AB_prime
);

  wire not_1_out, not_2_out, or_1_out;

  not not_1 (not_1_out, A);
  not not_2 (not_2_out, B);
  and and_1 (A_prime_B, not_1_out, B);
  and and_2 (AB_prime, A, not_2_out);
  not not_3 (A_ExOR_B, or_1_out);
  or or_1 (or_1_out, A_prime_B, AB_prime);

  // Notes on the sheet:
  //   2107086
endmodule

module _2_bit_comparator (
  input  A1,
  input  A0,
  input  B1,
  input  B0,
  output A_B,
  output A_B_2,
  output A_B_3
);

  wire and_1_out, and_3_out, exor_1_a_exor_b, exor_1_a_prime_b, exor_1_ab_prime, exor_2_a_exor_b,
       exor_2_a_prime_b, exor_2_ab_prime;

  ExOR exor_1 (.A(A1), .B(B1), .A_prime_B(exor_1_a_prime_b), .A_ExOR_B(exor_1_a_exor_b), .AB_prime(exor_1_ab_prime));
  ExOR exor_2 (.A(A0), .B(B0), .A_prime_B(exor_2_a_prime_b), .A_ExOR_B(exor_2_a_exor_b), .AB_prime(exor_2_ab_prime));
  and and_1 (and_1_out, exor_1_a_exor_b, exor_2_a_prime_b);
  and and_2 (A_B_2, exor_1_a_exor_b, exor_2_a_exor_b);
  and and_3 (and_3_out, exor_2_ab_prime, exor_1_a_exor_b);
  or or_1 (A_B, exor_1_a_prime_b, and_1_out);
  or or_2 (A_B_3, and_3_out, exor_1_ab_prime);

  // Notes on the sheet:
  //   2107086
endmodule

module _4_bit_comparator (
  input  A3,
  input  A2,
  input  A1,
  input  A0,
  input  B3,
  input  B2,
  input  B1,
  input  B0,
  output A_B,
  output A_B_2,
  output A_B_3
);

  wire and_1_out, and_2_out, n2_bit_comparator_1_a_b, n2_bit_comparator_1_a_b_2, n2_bit_comparator_1_a_b_3,
       n2_bit_comparator_2_a_b, n2_bit_comparator_2_a_b_2, n2_bit_comparator_2_a_b_3;

  _2_bit_comparator u_2_bit_comparator_1 (
    .A1(A3), .A0(A2), .B1(B3), .B0(B2), .A_B(n2_bit_comparator_1_a_b), .A_B_2(n2_bit_comparator_1_a_b_2),
    .A_B_3(n2_bit_comparator_1_a_b_3));
  _2_bit_comparator u_2_bit_comparator_2 (
    .A1(A1), .A0(A0), .B1(B1), .B0(B0), .A_B(n2_bit_comparator_2_a_b), .A_B_2(n2_bit_comparator_2_a_b_2),
    .A_B_3(n2_bit_comparator_2_a_b_3));
  and and_1 (and_1_out, n2_bit_comparator_1_a_b_2, n2_bit_comparator_2_a_b);
  and and_2 (and_2_out, n2_bit_comparator_1_a_b_2, n2_bit_comparator_2_a_b_3);
  or or_1 (A_B, n2_bit_comparator_1_a_b, and_1_out);
  and and_3 (A_B_2, n2_bit_comparator_1_a_b_2, n2_bit_comparator_2_a_b_2);
  or or_2 (A_B_3, and_2_out, n2_bit_comparator_1_a_b_3);

  // Notes on the sheet:
  //   2107086
endmodule
