// Logisim project BCD to Excess 3 circuit 2107086.circ as structural Verilog: 3 circuits, main circuit main
module down_counter (
  output out_1,
  output out_2,
  output out_3
);

  wire clock_1_out, DA0_qn, or_1_out, xnor_1_out, xnor_2_out;

  Clock clock_1 (.out(clock_1_out));
  D_Flip_Flop DA0 (.clk(clock_1_out), .D(DA0_qn), .Q(out_3), .Qn(DA0_qn));  // open: preset, en, reset
  xnor xnor_1 (xnor_1_out, out_3, out_2);
  D_Flip_Flop DA1 (.clk(clock_1_out), .D(xnor_1_out), .Q(out_2));  // open: Qn, preset, en, reset
  or or_1 (or_1_out, out_2, out_3);
  D_Flip_Flop DA2 (.clk(clock_1_out), .D(xnor_2_out), .Q(out_1));  // open: Qn, preset, en, reset
  xnor xnor_2 (xnor_2_out, out_1, or_1_out);
endmodule

module main (
);


  // Notes on the sheet:
  //   2107086
endmodule

module BCD_to_Excess_3 (
  input  B3,
  input  B2,
  input  B1,
  input  B0,
  output E3,
  output E2,
  output E1,
  output E0
);

  wire and_1_out, or_1_out, xor_1_out;

  or or_1 (or_1_out, B0, B1);
  and and_1 (and_1_out, B2, or_1_out);
  xor xor_1 (xor_1_out, B1, B0);
  or or_2 (E3, B3, and_1_out);
  xor xor_2 (E2, B2, or_1_out);
  not not_1 (E1, xor_1_out);
  not not_2 (E0, B0);

  // Notes on the sheet:
  //   2107086
endmodule
