// Logisim project BCD to Hex 7 segment circuit 2107086.circ as structural Verilog: 3 circuits, main circuit main
module down_counter (
  output out_1,
  output out_2,
  output out_3
);

  wire clock_1_out, DA0_qn, or_1_out, xnor_1_out, xnor_2_out;

  Clock clock_1 (.out(clock_1_out));
  D_Flip_Flop DA0 (.clk(clock_1_out), .D(DA0_qn), .Q(out_3), .Qn(DA0_qn));  // open: preset, en, reset
  xnor xnor_1 (xnor_1_out, out_3, out_2);
  D_Flip_Flop DA1 (.clk(clock_1_out), .D(xnor_1_out), .Q(out_2));  // open: Qn, preset, en, reset
  or or_1 (or_1_out, out_2, out_3);
  D_Flip_Flop DA2 (.clk(clock_1_out), .D(xnor_2_out), .Q(out_1));  // open: Qn, preset, en, reset
  xnor xnor_2 (xnor_2_out, out_1, or_1_out);
endmodule

module main (
  input  D,
  input  C,
  input  B,
  input  A
);

  wire bcd_to_hex_7_segment_1_a_2, bcd_to_hex_7_segment_1_b_2, bcd_to_hex_7_segment_1_c_2,
       bcd_to_hex_7_segment_1_d_2, bcd_to_hex_7_segment_1_e, bcd_to_hex_7_segment_1_f,
       bcd_to_hex_7_segment_1_g;

  BCD_to_Hex_7_Segment bcd_to_hex_7_segment_1 (
    .A(A), .B(B), .C(C), .D(D), .a_2(bcd_to_hex_7_segment_1_a_2), .b_2(bcd_to_hex_7_segment_1_b_2),
    .c_2(bcd_to_hex_7_segment_1_c_2), .d_2(bcd_to_hex_7_segment_1_d_2), .e(bcd_to_hex_7_segment_1_e),
    .f(bcd_to_hex_7_segment_1_f), .g(bcd_to_hex_7_segment_1_g));
  _7_Segment_Display u_7_segment_display_1 (
    .g(bcd_to_hex_7_segment_1_g), .f(bcd_to_hex_7_segment_1_f), .a(bcd_to_hex_7_segment_1_a_2),
    .b(bcd_to_hex_7_segment_1_b_2), .e(bcd_to_hex_7_segment_1_e), .d(bcd_to_hex_7_segment_1_d_2),
    .c(bcd_to_hex_7_segment_1_c_2));  // open: dp

  // Notes on the sheet:
  //   2107086
endmodule

module BCD_to_Hex_7_Segment (
  input  A,
  input  B,
  input  C,
  input  D,
  output a_2,
  output b_2,
  output c_2,
  output d_2,
  output e,
  output f,
  output g
);

  wire A_prime_B_out, A_prime_B_prime_C_out, A_prime_B_prime_out, A_prime_BC_prime_out, A_prime_BD_out,
       A_prime_C_out, A_prime_CD_out, A_prime_CD_prime_out, A_prime_D_out, AB_prime_C_prime_out,
       AB_prime_D_out, AB_prime_out, ABD_out, AC_out, AC_prime_out, AD_out, AD_prime_out, B_prime_C_out,
       B_prime_C_prime_D_prime_out, B_prime_D_prime_out, BC_out, BC_prime_D_out, BCD_prime_out, BD_prime_out,
       C_prime_D_prime_2_out, C_prime_D_prime_out, CD_prime_out, not_1_out, not_2_out, not_3_out, not_4_out;

  not not_1 (not_1_out, A);
  not not_2 (not_2_out, B);
  not not_3 (not_3_out, C);
  not not_4 (not_4_out, D);
  and B_prime_D_prime (B_prime_D_prime_out, not_2_out, not_4_out);
  and A_prime_C (A_prime_C_out, not_1_out, C);
  and BC (BC_out, B, C);
  and AD_prime (AD_prime_out, A, not_4_out);
  and AB_prime_C_prime (AB_prime_C_prime_out, A, not_2_out, not_3_out);
  and A_prime_BD (A_prime_BD_out, not_1_out, B, D);
  and AC_prime (AC_prime_out, A, not_3_out);
  and A_prime_B_prime (A_prime_B_prime_out, not_1_out, not_2_out);
  and C_prime_D_prime (C_prime_D_prime_out, not_3_out, not_4_out);
  and A_prime_CD (A_prime_CD_out, not_1_out, C, D);
  and A_prime_D (A_prime_D_out, not_1_out, D);
  and A_prime_B (A_prime_B_out, not_1_out, B);
  and AB_prime (AB_prime_out, A, not_2_out);
  and B_prime_C_prime_D_prime (B_prime_C_prime_D_prime_out, not_2_out, not_3_out, not_4_out);
  and A_prime_B_prime_C (A_prime_B_prime_C_out, not_1_out, not_2_out, C);
  and A_prime_CD_prime (A_prime_CD_prime_out, not_1_out, C, not_4_out);
  and BC_prime_D (BC_prime_D_out, B, not_3_out, D);
  and BCD_prime (BCD_prime_out, B, C, not_4_out);
  and AB_prime_D (AB_prime_D_out, A, not_2_out, D);
  and CD_prime (CD_prime_out, C, not_4_out);
  and AC (AC_out, A, C);
  and ABD (ABD_out, A, B, D);
  and A_prime_BC_prime (A_prime_BC_prime_out, not_1_out, B, not_3_out);
  and C_prime_D_prime_2 (C_prime_D_prime_2_out, not_3_out, not_4_out);
  and BD_prime (BD_prime_out, B, not_4_out);
  and AD (AD_out, A, D);
  and B_prime_C (B_prime_C_out, not_2_out, C);
  or u_a (a_2, B_prime_D_prime_out, A_prime_C_out, BC_out, AD_prime_out, AB_prime_C_prime_out, A_prime_BD_out);
  or u_b (b_2, AC_prime_out, B_prime_D_prime_out, A_prime_B_prime_out, C_prime_D_prime_out, A_prime_CD_out);
  or u_c (c_2, not_3_out, A_prime_D_out, A_prime_B_out, AB_prime_out);
  or u_d (d_2, B_prime_C_prime_D_prime_out, A_prime_B_prime_C_out, A_prime_CD_prime_out, AC_prime_out, BC_prime_D_out, BCD_prime_out, AB_prime_D_out);
  or u_e (e, B_prime_D_prime_out, CD_prime_out, AC_out, ABD_out);
  or u_f (f, AB_prime_out, BD_prime_out, AC_out, A_prime_BC_prime_out, C_prime_D_prime_2_out);
  or u_g (g, A_prime_BC_prime_out, CD_prime_out, AB_prime_out, AD_out, B_prime_C_out);

  // Notes on the sheet:
  //   2107086
endmodule
